# Fritzing sketch Receiver robot scheme (saved by Fritzing 0.9.3b)
breadboards: 1

parts:
  Часть1 = NRF24L01+ Breakout Board
  Часть3 = Arduino Nano (Rev3.0)
  U2 = LIPO-2000mAh [package=lipo-2000]
  U3 = L9110 H-bridge module [part_number="L9110 H-bridge"]
  M4 = DC Motor
  M3 = DC Motor

nets:
  GND: Часть1.GND, Часть3.GND, U2.-, U3.GND
  VCC: Часть1.VCC, Часть3.3V3
  N1: Часть1.CE, Часть3.D7
  N2: Часть1.CS, Часть3.D8
  N3: Часть1.SCK, Часть3.D13/SCK
  N4: Часть1.MOSI, Часть3.D11/MOSI
  N5: Часть1.MISO, Часть3.D12/MISO
  N6: Часть3.D5, U3.B-IA
  N7: Часть3.D6, U3.B-IB
  N8: Часть3.D9, U3.A-IA
  N9: Часть3.D10, U3.A-IB
  5V: Часть3.5V, U2.+, U3.VCC
  N10: U3.MOTOR_A-A, M4.pin_2
  N11: U3.MOTOR_A-B, M4.pin_1
  N12: U3.MOTOR_B-B, M3.pin_2
